# Fritzing sketch proto_layout_v1 (saved by Fritzing 0.9.3b)
breadboards: 1

parts:
  S1 = Pushbutton [package="[THT]"]
  Part2 = Arduino Ethernet Shield (Rev3)
  R1 = Resistor [tolerance=±5% resistance=10k package=THT]
  LED1 = LED - 5mm [color="Red (633nm)" package="5 mm [THT]"]

nets:
  N1: S1.Pin_1, S1.Pin_2, Part2.D7, R1.Pin_0
  N2: S1.Pin_3, S1.Pin_4
  N3: Part2.D8, LED1.anode
  N4: Part2.GND, R1.Pin_1, LED1.cathode
